// Digital circuit design2.dig as structural Verilog
module design2 (
  input  c1,
  input  c0,
  input  clk,
  input  reset,
  output q2,
  output q1,
  output q0,
  output MG,
  output MY,
  output MR,
  output SG,
  output SY,
  output SR
);

  wire and_1_out, and_2_out, and_3_out, and_4_out, and_5_out, and_6_out, and_7_out, and_8_out, and_9_out,
       and_10_out, and_11_out, and_12_out, and_13_out, and_14_out, and_15_out, and_16_out, and_17_out,
       and_18_out, and_19_out, and_20_out, and_21_out, c0b, c1b, or_3_out, or_4_out, or_5_out, q0b, q1b, q2b;

  not not_1 (c1b, c1);
  not not_2 (c0b, c0);
  and and_1 (and_1_out, q2b, q1, q0, c1b, c0b);
  and and_2 (and_2_out, q2b, q1b, q0, c1);
  and and_3 (and_3_out, q1, q0b, c0);
  and and_4 (and_4_out, q2, q1b, q0b, c1b);
  and and_5 (and_5_out, c1, c0);
  and and_6 (and_6_out, q2, c0);
  and and_7 (and_7_out, q2b, c0);
  and and_8 (and_8_out, q2b, q1b, q0);
  and and_9 (and_9_out, q2b, q1, q0b, c1b);
  and and_10 (and_10_out, c1, c0);
  and and_11 (and_11_out, q1b, q0, c0);
  and and_12 (and_12_out, q2b, q0b, c0b);
  and and_13 (and_13_out, c1, c0b);
  and and_14 (and_14_out, q2b, q1, q0b, c1b);
  and and_15 (and_15_out, q2, c1b, c0);
  and and_16 (and_16_out, q2, q1b, q0b, c1b);
  and and_17 (and_17_out, q2, q1, q0b, c0);
  and and_18 (and_18_out, q2b, q1b, q0);
  and and_19 (and_19_out, q2, q1, q0b);
  and and_20 (and_20_out, q2b, q0b);
  and and_21 (and_21_out, q1b, q0);
  and and_22 (MG, q2b, q1b, q0b);
  or or_1 (MY, and_18_out, and_19_out);
  xor xor_1 (MR, q2, q1);
  and and_23 (SG, q2b, q1, q0);
  and and_24 (SY, q2, q0b);
  or or_2 (SR, and_20_out, and_21_out);
  or or_3 (or_3_out, and_1_out, and_2_out, and_3_out, and_4_out, and_5_out, and_6_out);
  or or_4 (or_4_out, and_7_out, and_8_out, and_9_out, and_10_out, and_11_out);
  or or_5 (or_5_out, and_12_out, and_13_out, and_14_out, and_15_out, and_16_out, and_17_out);
  D_FF_AS u_Q2 (.Set(1'b0), .D(or_3_out), .C(clk), .Clr(reset), .Q(q2), .nQ(q2b));
  D_FF_AS u_Q1 (.Set(1'b0), .D(or_4_out), .C(clk), .Clr(reset), .Q(q1), .nQ(q1b));
  D_FF_AS u_Q0 (.Set(1'b0), .D(or_5_out), .C(clk), .Clr(reset), .Q(q0), .nQ(q0b));
  LED led_1 (.in(MR));
  LED led_2 (.in(MY));
  LED led_3 (.in(MG));
  LED led_4 (.in(SR));
  LED led_5 (.in(SY));
  LED led_6 (.in(SG));
endmodule
